# Fritzing sketch schematic (saved by Fritzing 0.9.9b)

parts:
  M1 = ESP32-C3-DevKitC-02 [part_number=ESP32-C3-DevKitC-02]
  Tiny_RTC1 = Tiny RTC
  IC1 = Nextion SPI 2.4" LCD NX3224T024_011
  JACK1 = 2.1mm Barrel Jack with Terminal Block
  SG1 = Buzzer 12mm [part_number=COM-07950 package=buzzer-12mm-ns]

nets:
  N1: M1.19, IC1.pin3
  N2: M1.18, IC1.pin2
  GND: M1.GND, Tiny_RTC1.GND, IC1.GND, JACK1.NEG, SG1.2
  N3: M1.4, Tiny_RTC1.SDA
  N4: M1.5, Tiny_RTC1.SCL
  N5: M1.7, SG1.1
  VCC: M1.5V, Tiny_RTC1.VCC, IC1.VCC, JACK1.POS

notes:
  DC 5V Supply

custom parts:
  ESP32-C3-DevKitC-02: Esp32-C3 DevKitC 02 is one of the development board created by Espressif. It is based on the ESP32 microcontroller that boasts Wifi, Bluetooth, Ethernet and Low Power support all in a single chip. (vanepp) Feb 2021: converted to ESP32-C3-DevKitC-02. This chip is 30pins long (2 x15) and 11 pins width.
  Tiny RTC: Tiny RTC I2C module DS1370Z RTC and AT24C32 EEPROM
  Buzzer 12mm: Buzzer 12mm Spark Fun Electronics SKU : Comp-Buzzer Through hole This is a small 12mm round speaker that operates around the audible 2kHz range. You can use these speakers to create simple music or user interfaces. This is not a true piezoelectric speaker but behaves similarly. Instead of a piezoelectric crystal that vibrates with an electric current, this tiny speaker uses an electromagnet to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
